// Logisim project MicroProcessor.circ as structural Verilog: 39 circuits, main circuit Processor
module ALSU (
  input  [15:0] A,
  input  [15:0] B,
  input  [15:0] D,
  input  [15:0] Instruction,
  input  [4:0] Flags,
  output [15:0] Data,
  output [4:0] Flags_2,
  output [15:0] T
);

  wire [4:0] _0011_F, ADD_F, AND_F, DEC_F, INC_F, LSL8_F, LSL_F, LSR8_F, LSR_F, MULT_F, multiplexer_1_out,
       OR_F, RSTRF, SETF_CLRF, SUB_F, XOR_F;
  wire [15:0] _0011, ADD, AND, DEC, INC, LSL, LSL8, LSR, LSR8, MULT, OR, SAVEF, SETHI, SETLO, SUB, T_t, XOR;

  LSL u_LSL (.Rd(B), .Flags(Flags), .shr_rolc_Rd(LSL), .Flags_2(LSL_F));
  LSR u_LSR (.Rd(B), .Flags(Flags), .shl_rolc_Rb(LSR), .Flags_2(LSR_F));
  LSL8 u_LSL8 (.Rd(B), .Flags(Flags), .shr_rolc_Rd(LSL8), .Flags_2(LSL8_F));
  LSR8 u_LSR8 (.Rd(B), .Flags(Flags), .shr_rolc_Rd(LSR8), .Flags_2(LSR8_F));
  SETF_CLRF u_SETF_CLRF (._8__3_0({Instruction[8], Instruction[3:0]}), ._11(Instruction[11]), .Flags(SETF_CLRF));
  SAVEF u_SAVEF (.Flags(Flags), .Output(SAVEF));
  RSTRF u_RSTRF (.Rd(D), .New_Flags(RSTRF));
  INC u_INC (.Rd(D), .Epsilon(Instruction[5:0]), .Rd___e(INC), .Flags(INC_F));
  DEC u_DEC (.Rd(D), .Epsilon(Instruction[5:0]), .Rd___e(DEC), .Flags(DEC_F));
  AND u_AND (.Operand_1(A), .Operand_2(B), .Flags(Flags), .Output(AND), .Flags_2(AND_F));
  OR or_1 (.A(A), .B(B), .in_3(Flags), .XOR(OR), .Flags(OR_F));
  ADD u_ADD (.Input_1(A), .Sum(ADD), .Input_1_2(B), .Flags(Flags), .Flags_2(ADD_F));
  SUBTRACT SUBTRACT (.Ra(A), .Ra_Rb__c_F4_prime(SUB), .Rb(B), .Flags(Flags), .Flags_2(SUB_F));
  MULT u_MULT (.A(A), .B(B), .Flags(Flags), .Product(MULT), .T(T_t), .Flags_2(MULT_F));
  XOR u_XOR (.A(A), .B(B), .in_3(Flags), .XOR(XOR), .Flags(XOR_F));
  SETLO u_SETLO (.Value(Instruction[7:0]), .SETLO(SETLO));
  SETHI u_SETHI (.Value(Instruction[7:0]), .Register_Data(D), .SETHI(SETHI));
  Multiplexer #(.select(4), .width(5), .enable("false")) multiplexer_1 (
    .in8(RSTRF), .out(multiplexer_1_out), .sel(Instruction[3:0]));  // open: in0, in1, in2, in3, in4, in5, in6, in7, in9, in10, in11, in12, in13, in14, in15
  Multiplexer #(.select(4), .width(16)) multiplexer_2 (
    .in0(LSL), .in1(LSR), .in2(LSL8), .in3(LSR8), .in7(SAVEF), .in8(INC), .in9(INC), .in10(INC), .in11(INC),
    .in12(DEC), .in13(DEC), .in14(DEC), .in15(DEC), .out(_0011), .sel(Instruction[7:4]));  // open: in4, in5, in6, en
  Multiplexer #(.select(4), .width(5)) multiplexer_3 (
    .in0(LSL_F), .in1(LSR_F), .in2(LSL8_F), .in3(LSR8_F), .in6(SETF_CLRF), .in7(multiplexer_1_out),
    .in8(INC_F), .in9(INC_F), .in10(INC_F), .in11(INC_F), .in12(DEC_F), .in13(DEC_F), .in14(DEC_F),
    .in15(DEC_F), .out(_0011_F), .sel(Instruction[7:4]));  // open: in4, in5, en
  Multiplexer #(.select(4), .width(16)) multiplexer_4 (
    .in3(_0011), .in8(AND), .in9(OR), .in10(ADD), .in11(SUB), .in12(MULT), .in13(XOR), .in14(SETLO),
    .in15(SETHI), .out(Data), .sel(Instruction[15:12]));  // open: in0, in1, in2, in4, in5, in6, in7, en
  Multiplexer #(.select(4), .width(5)) multiplexer_5 (
    .in3(_0011_F), .in8(AND_F), .in9(OR_F), .in10(ADD_F), .in11(SUB_F), .in12(MULT_F), .in13(XOR_F),
    .out(Flags_2), .sel(Instruction[15:12]));  // open: in0, in1, in2, in4, in5, in6, in7, in14, in15, en
  Multiplexer #(.select(4), .width(16)) multiplexer_6 (
    .in12(T_t), .out(T), .sel(Instruction[15:12]));  // open: in0, in1, in2, in3, in4, in5, in6, in7, in8, in9, in10, in11, in13, in14, in15, en

  // Other names for the same wires on the sheet: epsilon[5:0] = Instruction[5:0]; I[15:0] = Instruction;
  //   Last4[3:0] = Instruction[3:0]; S_C_Flags[4:0] = {Instruction[8], Instruction[3:0]}; Set[7:0] = Instruction[7:0];
  //   Select[3:0] = Instruction[7:4]; S_C = Instruction[11]; Opcode[3:0] = Instruction[15:12]

  // Notes on the sheet:
  //   Inputs
  //   Modules
  //   1100 Multiplexers
  //   Opcode Multiplexers
endmodule

module SETLO (
  input  [7:0] Value,
  output [15:0] SETLO
);

  assign SETLO = {{8{1'b0}}, Value};  // Bit_Extender bit_extender_1
endmodule

module SETHI (
  input  [7:0] Value,
  input  [15:0] Register_Data,
  output [15:0] SETHI
);


  assign SETHI = {Value, Register_Data[7:0]};
endmodule

module ADD (
  input  [15:0] Input_1,
  input  [15:0] Input_1_2,
  input  [4:0] Flags,
  output [15:0] Sum,
  output [4:0] Flags_2
);

  wire CB_carry_2;

  Carry_Block CB (.Carry(Flags[3]), .Carry_Block(Flags[4]), .Carry_2(CB_carry_2));
  Adder #(.width(16)) adder_1 (.a(Input_1), .b(Input_1_2), .out(Sum), .cin(CB_carry_2), .cout(Flags_2[3]));
  Overflow_Check overflow_check_1 (
    .Sign_Input1(Input_1[15]), .Sign_Input2(Input_1_2[15]), .Sign_Output(Sum[15]), .Overflow(Flags_2[2]));
  Comparator #(.width(16)) comparator_1 (.a(Sum), .b({16{1'b0}}), .eq(Flags_2[1]), .lt(Flags_2[0]));  // open: gt
endmodule

// SUB
module SUBTRACT (
  input  [15:0] Ra,
  input  [15:0] Rb,
  input  [4:0] Flags,
  output [15:0] Ra_Rb__c_F4_prime,
  output [4:0] Flags_2
);

  wire CB_carry_2;

  Carry_Block CB (.Carry(Flags[3]), .Carry_Block(Flags[4]), .Carry_2(CB_carry_2));
  Subtractor #(.width(16)) subtractor_1 (.a(Ra), .b(Rb), .out(Ra_Rb__c_F4_prime), .bin(CB_carry_2), .bout(Flags_2[3]));
  Overflow_Check overflow_check_1 (
    .Sign_Input1(Ra[15]), .Sign_Input2(Rb[15]), .Sign_Output(Ra_Rb__c_F4_prime[15]), .Overflow(Flags_2[2]));
  Comparator #(.width(16)) comparator_1 (
    .a(Ra_Rb__c_F4_prime), .b({16{1'b0}}), .eq(Flags_2[1]), .lt(Flags_2[0]));  // open: gt
endmodule

module LSL (
  input  [15:0] Rd,
  input  [4:0] Flags,
  output [15:0] shr_rolc_Rd,
  output [4:0] Flags_2
);

  wire [15:15] shifter_1_out;

  Shifter #(.width(16)) shifter_1 (.in(Rd), .\dist (4'b0000), .out({shifter_1_out[15], shr_rolc_Rd[15:1]}));
  Carry_Block carry_block_1 (.Carry(Flags[3]), .Carry_Block(Flags[4]), .Carry_2(shr_rolc_Rd[0]));

  assign Flags_2[3] = Rd[15];
endmodule

module LSR (
  input  [15:0] Rd,
  input  [4:0] Flags,
  output [15:0] shl_rolc_Rb,
  output [4:0] Flags_2
);

  wire [0:0] shifter_1_out;

  Shifter #(.width(16), .shift("lr")) shifter_1 (
    .in(Rd), .\dist (4'b0000), .out({shl_rolc_Rb[14:0], shifter_1_out[0]}));
  Carry_Block carry_block_1 (.Carry(Flags[3]), .Carry_Block(Flags[4]), .Carry_2(shl_rolc_Rb[15]));

  assign Flags_2[3] = Rd[0];
endmodule

module AND (
  input  [15:0] Operand_1,
  input  [15:0] Operand_2,
  input  [4:0] Flags,
  output [15:0] Output,
  output [4:0] Flags_2
);

  assign Output = Operand_1 & Operand_2;  // AND_Gate and_1, 16 bits wide
  Comparator #(.width(16)) comparator_1 (.a(Output), .b({16{1'b0}}), .eq(Flags_2[1]), .lt(Flags_2[0]));  // open: gt
endmodule

module Processor (
);

  wire _13, and_1_out, and_2_out, and_3_out, and_5_out, and_6_out, and_7_out, button_1_out, CLK, clock_1_out,
       comparator_2_eq, comparator_4_lt, comparator_5_gt, comparator_6_eq, comparator_7_eq, get_char, isLoad,
       K1_Enable, K2_Enable, Keyboard_Interrupt, keyboardmemorystore_1_clk_2, keyboardmemorystore_1_clr_2,
       keyboardmemorystore_1_load_2, keyboardmemorystore_1_select_2, keyboardmemorystore_1_store_2,
       Keystroke_1, Keystroke_2, L_S, NewPrivilege, not_1_out, not_2_out, not_3_out, not_4_out, or_3_out,
       or_4_out, Privilege, put_char, R2_0, Reset, ThreadError, ThreadSwitch;
  wire [1:0] OS_Select;
  wire [3:0] _3_0, _11_8;
  wire [3:2] _15_12;
  wire [4:0] ALSU_Flags, Flags, LOAD_Flags, multiplexer_2_out, multiplexer_3_out, Thread_Flags;
  wire [4:4] _12__7_4;
  wire [6:0] keyboard_1_data, keyboard_2_data;
  wire [7:4] _7_0;
  wire [15:0] A, ALSU_Out, B, bit_extender_1_out, bit_extender_2_out, C_R_A, C_R_B, C_R_FP, counter_1_q, CT,
       D, Data_D, Data_T, FP, Interrupt_PC, Keyboard, keyboardmemorystore_1_new_address,
       keyboardmemorystore_1_new_data, KillThread, KillThreadError, load_store_1_rb___o, Memory_Out, PC,
       Registers_r0, Registers_r1, Registers_r2, Registers_r3, Registers_r4, Registers_r5, Registers_r6,
       Registers_r7, Registers_r8, Registers_r9, Registers_r10, Registers_r11, Registers_r12, Registers_r13,
       Registers_r14, Registers_r15, StartThread, Thread_PC, TSLocation, TTY1, TTY2;

  Keyboard #(.buflen(16)) keyboard_1 (
    .clk(CLK), .re(K1_Enable), .clr(Reset), .avail(Keystroke_1), .data(keyboard_1_data));
  Keyboard #(.buflen(16)) keyboard_2 (
    .clk(CLK), .re(K2_Enable), .clr(Reset), .avail(Keystroke_2), .data(keyboard_2_data));
  Comparator comparator_1 (.a(8'h11), .b({_15_12, _13, _12__7_4[4], _11_8}), .eq(put_char));  // open: gt, lt
  and and_1 (and_1_out, get_char, not_1_out);
  not not_1 (not_1_out, R2_0);
  and and_2 (and_2_out, get_char, R2_0);
  Control_Flow Control_Flow (
    .CLK(CLK), ._15_12({_15_12, _13, _12__7_4[4]}), ._11_8(_11_8), ._7_0({_7_0, _3_0}), .Reset(Reset), .B(B),
    .Flags(Flags), .I(Interrupt_PC), .Address(PC), .Keystroke(Keyboard_Interrupt), .Thread_PC(Thread_PC),
    .ThreadSwitch(ThreadSwitch), .ThreadService(TSLocation), .StartThread(StartThread),
    .KillThread(KillThread), .OS_Select(OS_Select), .KillThreadError(KillThreadError),
    .ThreadError(ThreadError), .Privileges(Privilege));
  // Probe on PC
  or or_1 (K1_Enable, 1'b0, and_1_out);
  or or_2 (K2_Enable, 1'b0, and_2_out);
  Counter #(.width(16), .max('hffff)) counter_1 (
    .count(1'b1), .Q(counter_1_q), .clk(CLK), .clr(button_1_out));  // open: load, D, carry
  Button button_1 (.out(button_1_out));
  Comparator #(.width(16)) comparator_2 (.a(counter_1_q), .b({16{1'b1}}), .eq(comparator_2_eq));  // open: gt, lt
  // Probe on Registers_r0
  // Probe on Registers_r1
  // Probe on Registers_r2
  // Probe on Registers_r3
  // Probe on Registers_r4
  // Probe on Registers_r5
  // Probe on Registers_r6
  // Probe on Registers_r7
  assign bit_extender_1_out = {{9{1'b0}}, keyboard_1_data};  // Bit_Extender bit_extender_1
  assign bit_extender_2_out = {{9{1'b0}}, keyboard_2_data};  // Bit_Extender bit_extender_2
  Comparator comparator_3 (.a(8'h1), .b({_15_12, _13, _12__7_4[4], _11_8}), .eq(get_char));  // open: gt, lt
  ROM #(.addrWidth(16), .dataWidth(16)) rom_1 (
    .addr(PC), .data({_15_12, _13, _12__7_4[4], _11_8, _7_0, _3_0}));  // open: sel
  Button button_2 (.out(Reset));
  Clock clock_1 (.out(clock_1_out));
  assign CLK = not_2_out ? clock_1_out : 1'bz;  // Controlled_Buffer controlled_buffer_1
  not not_2 (not_2_out, comparator_2_eq);
  // Probe on Registers_r8
  // Probe on Registers_r9
  // Probe on Registers_r10
  Registers Registers (
    .CLK(CLK), .A(_7_0), .B(_3_0), .D(_11_8), .Data_A(C_R_A), .Data_T(Data_T),
    .Instruction({_15_12, _13, _12__7_4[4], _11_8, _7_0, _3_0}), .Reset(Reset), .A_2(A), .B_2(B), .D_2(D),
    .R0(Registers_r0), .R1(Registers_r1), .R2(Registers_r2), .R3(Registers_r3), .R4(Registers_r4),
    .R5(Registers_r5), .R6(Registers_r6), .R7(Registers_r7), .R8(Registers_r8), .R9(Registers_r9),
    .R10(Registers_r10), .R11(Registers_r11), .R12(Registers_r12), .R13(Registers_r13), .R14(Registers_r14),
    .R15(Registers_r15), .FP(FP), .Data_B(C_R_B), .Data_D(Data_D), .Data_FP(C_R_FP), .Keyboard(Keyboard),
    .K1(TTY1), .K1_2(TTY2), .R2_2(R2_0), .PC(PC), .Flags(Flags), .ThreadSwitch(ThreadSwitch),
    .Thread_Flags(Thread_Flags), .Thread_PC(Thread_PC), .TSLocation(TSLocation), .CurrentThread(CT),
    .StartThread(StartThread), .KillThread(KillThread), .OS_Select(OS_Select),
    .KillThreadError(KillThreadError), .Privileges(Privilege), .New_Flags(NewPrivilege));
  // Probe on Registers_r11
  // Probe on Registers_r12
  // Probe on Registers_r13
  // Probe on Registers_r14
  // Probe on Registers_r15
  // Probe on Thread_PC
  // Probe on Thread_Flags
  // Probe on CT
  // Probe on TSLocation
  // Probe on StartThread
  // Probe on KillThread
  // Probe on OS_Select
  // Probe on KillThreadError
  Multiplexer #(.width(16)) multiplexer_1 (
    .in0(bit_extender_1_out), .in1(bit_extender_2_out), .out(Keyboard), .sel(R2_0), .en(get_char));
  Counter counter_2 (.count(Keyboard_Interrupt), .clk(CLK));  // open: load, D, Q, carry, clr
  New_Keyboard_Input new_keyboard_input_1 (
    .CLK(CLK), .clr(Reset), .K1_Input(Keystroke_1), .K2_Input(Keystroke_2),
    .New_Interrupt(Keyboard_Interrupt), .Opcode({_15_12, _13, _12__7_4[4]}), .Instruction(_11_8));  // open: New_Keyboard_Input, Keyboard_Empty
  CALL_RETURN_Interrupt CALL_RETURN (
    .PC(PC), .Ra(A), .Rb(B), .FP(FP), .PC_2(Interrupt_PC), .Ra_2(C_R_A), .Rb_2(C_R_B), .Fp_2(C_R_FP),
    .Opcode({_15_12, _13, _12__7_4[4]}), .Instruction(_11_8), .Interrupt(_3_0));
  not not_3 (not_3_out, R2_0);
  TTY tty_1 (.data(TTY1[6:0]), .clk(CLK), .we(and_3_out), .clr(Reset));
  and and_3 (and_3_out, put_char, not_3_out);
  ALSU ALSU (
    .A(A), .B(B), .D(D), .Instruction({_15_12, _13, _12__7_4[4], _11_8, _7_0, _3_0}), .Flags(Flags),
    .Data(ALSU_Out), .Flags_2(ALSU_Flags), .T(Data_T));
  LOAD_STORE load_store_1 (.Rb(B), .Offset({_12__7_4[4], _7_0}), .Rb___o(load_store_1_rb___o));
  Comparator #(.width(4)) comparator_4 (
    .a(4'b1000), .b({_15_12, _13, _12__7_4[4]}), .lt(comparator_4_lt));  // open: gt, eq
  and and_4 (L_S, comparator_4_lt, comparator_5_gt);
  Comparator #(.width(4)) comparator_5 (
    .a({_15_12, _13, _12__7_4[4]}), .b(4'b0011), .gt(comparator_5_gt));  // open: eq, lt
  ThreadControl ThreadControl (
    .Instruction({_15_12, _13, _12__7_4[4], _11_8, _7_0, _3_0}), .CLK(CLK), .ThreadSwitch(ThreadSwitch),
    .in_3(Privilege));
  Comparator #(.width(16)) comparator_6 (
    .a({_15_12, _13, _12__7_4[4], _11_8, _7_0, _3_0}), .b(16'he002), .eq(comparator_6_eq));  // open: gt, lt
  Comparator #(.width(16)) comparator_7 (
    .a({_15_12, _13, _12__7_4[4], _11_8, _7_0, _3_0}), .b(16'he009), .eq(comparator_7_eq));  // open: gt, lt
  KeyboardMemoryStore keyboardmemorystore_1 (
    .load(not_4_out), .clr(Reset), .Address(load_store_1_rb___o), .K1_Input(Keystroke_1),
    .K2_Input(Keystroke_2), .select(L_S), .CLK(CLK), .select_2(keyboardmemorystore_1_select_2),
    .CLK_2(keyboardmemorystore_1_clk_2), .load_2(keyboardmemorystore_1_load_2),
    .clr_2(keyboardmemorystore_1_clr_2), .New_Address(keyboardmemorystore_1_new_address), .store(_13),
    .store_2(keyboardmemorystore_1_store_2), .Data(D), .New_Data(keyboardmemorystore_1_new_data), .CT(CT),
    .Instructions({_15_12, _13, _12__7_4[4], _11_8, _7_0, _3_0}), .ThreadError(ThreadError),
    .Privileges(Privilege));
  Multiplexer #(.width(5), .enable("false")) multiplexer_2 (
    .in0(LOAD_Flags), .in1(Thread_Flags), .out(multiplexer_2_out), .sel(or_3_out));
  or or_3 (or_3_out, and_5_out, and_6_out);
  and and_5 (and_5_out, comparator_6_eq, Privilege);
  and and_6 (and_6_out, comparator_7_eq, Privilege);
  not not_4 (not_4_out, _13);
  TTY tty_2 (.data(TTY2[6:0]), .clk(CLK), .we(and_7_out), .clr(Reset));
  and and_7 (and_7_out, put_char, R2_0);
  Multiplexer #(.width(5), .enable("false")) multiplexer_3 (
    .in0(ALSU_Flags), .in1(multiplexer_2_out), .out(multiplexer_3_out), .sel(or_4_out));
  or or_4 (or_4_out, and_5_out, and_6_out, isLoad);
  RAM #(.addrWidth(16), .dataWidth(16), .bus("separate")) ram_1 (
    .addr(keyboardmemorystore_1_new_address), .din(keyboardmemorystore_1_new_data), .data(Memory_Out),
    .str(keyboardmemorystore_1_store_2), .sel(keyboardmemorystore_1_select_2),
    .clk(keyboardmemorystore_1_clk_2), .ld(keyboardmemorystore_1_load_2), .clr(keyboardmemorystore_1_clr_2));
  Privileges Privileges (
    .in_1({_15_12, _13, _12__7_4[4], _11_8, _7_0, _3_0}), .in_2(CLK), .New_Flags(Privilege),
    .in_3(ThreadSwitch), .in_4(NewPrivilege), .in_5(ThreadError));
  Flags flags_1 (.CLK(CLK), .in_3(multiplexer_3_out), .out_4(Flags), .in_1(Reset));
  LOAD_Flags load_flags_1 (.in_1(Memory_Out), .in_2({_15_12, _13, _12__7_4[4]}), .out_3(LOAD_Flags));
  Comparator #(.width(3)) comparator_8 (.a({_15_12, _13}), .b(3'b010), .eq(isLoad));  // open: gt, lt
  Multiplexer #(.width(16)) multiplexer_4 (.in0(ALSU_Out), .in1(Memory_Out), .out(Data_D), .sel(L_S));  // open: en
  LED Sign (.in(Flags[0]));
  LED Zero (.in(Flags[1]));
  LED Overflow (.in(Flags[2]));
  LED Carry_Borrow (.in(Flags[3]));
  LED Carry_Block (.in(Flags[4]));

  // Other names for the same wires on the sheet: _7_0[3:0] = _3_0;
  //   Instruction[15:0] = {_15_12, _13, _12__7_4[4], _11_8, _7_0, _3_0}; _7_4[3:0] = _7_0; _12__7_4[3:0] = _7_0;
  //   _15_12[1:0] = {_13, _12__7_4[4]}

  // Notes on the sheet:
  //   Instruction Memory (ROM)
  //   contents of rom_1 (hex, n*v repeats v):
  //   3160 e1c3 f100 e21a f201 e346 f301 e446 f401 e006 e1ab f140 e200 f200 6201 e4b9 f440 e501 f500 6504
  //   e2ad f240 e601 f600 6602 e100 f100 e007 e004 e00a e101 f100 e230 f200 e008 e100 f100 e264 f200 3180
  //   3068 b021 ed27 fd00 190d e102 f100 e008 e101 f100 e242 f200 e008 e200 f200 e164 f100 3280 3068 b012
  //   ed39 fd00 190d e102 f100 e008 e101 f100 e254 f200 e008 e300 f300 e164 f100 3380 3068 b031 ed4b fd00
  //   190d e102 f100 e008 e101 f100 e273 f200 e008 e100 f100 e400 f400 e70c f700 3f84 410e 421e 432e 443e
  //   454e 3180 610e 611e 612e 613e 614e 3068 b071 ed60 fd00 190d e102 f100 e008 e101 f100 e285 f200 e008
  //   e500 f500 e264 f200 3580 3068 b025 ed7c fd00 190d e102 f100 e008 e101 f100 e29d f200 e008 e600 f600
  //   e264 f200 e8c8 f800 a8f8 4808 eea4 fe01 3680 3068 b026 ed8e fd00 190d e102 f100 e008 e101 f100 e2b5
  //   f200 e008 e700 f700 e264 f200 e8c8 f800 a8f8 6808 efa4 ff01 3780 3068 b027 eda6 fd00 190d e102 f100
  //   e008 e800 f800 e264 f200 3880 3068 b028 edb9 fd00 190d e102 f100 e008 0 6b0f 6c1f 6d2f ebab fb40
  //   4b0b ec11 fc00 cbbc ec01 fc40 accb 4b0f 610c 621c 632c 643c 654c 665c 676c 687c 698c 6a9c 6bac 4d2f
  //   6dcc 6edc 6fec 91c0 4c1f 6cb1 e000 6af1 7b01 e1ab f140 4101 3180 e308 f300 3068 b013 edf2 fd00 190d
  //   e100 f100 e2ad f240 a212 4202 ede8 fd00 180d e2ab f240 6102 e007 ebab fb40 4b0b ec11 fc00 cbbc ec01
  //   fc40 accb 4afc 5b0c e001 410c 421c 432c 443c 454c 465c 476c 487c 498c 4a9c 4bac 4dcc 4edc 4fec 4cbc
  //   e00a e002 611f 622f 633f 644f 655f 666f 6d7f e11e f100 3068 b021 ed2b fd01 150d ed46 fd01 100d e301
  //   f340 e4b9 f440 4504 3580 6504 35c0 e611 f600 c656 a363 62f3 e2ad f240 a252 e601 f600 6602 411f 422f
  //   433f 444f 455f 466f 4d7f e009 eaab fa40 4a0a ebad fb40 abab e900 f900 690b ede5 fd00 100d 0 e009
  //   l/s
  //   Opcode
  //   D
  //   A
  //   B
  //   o
  //   Offset
  //   Store
  //   Memory (RAM)
  //   Load
endmodule

module Two_s_Complement (
  input  [15:0] I,
  output [15:0] O
);

  wire [15:0] not_1_out;

  assign not_1_out = ~I;  // NOT_Gate not_1, 16 bits wide
  Adder #(.width(16)) adder_1 (.a(not_1_out), .b({16{1'b0}}), .out(O), .cin(1'b1));  // open: cout
endmodule

module Overflow_Check (
  input  Sign_Input1,
  input  Sign_Input2,
  input  Sign_Output,
  output Overflow
);

  wire xor_1_out, xor_2_out;

  xor xor_1 (xor_1_out, Sign_Input1, Sign_Output);
  xor xor_2 (xor_2_out, Sign_Input2, Sign_Output);
  and and_1 (Overflow, xor_1_out, xor_2_out);
endmodule

module Carry_Block (
  input  Carry,
  input  Carry_Block,
  output Carry_2
);

  Multiplexer multiplexer_1 (.in0(Carry), .in1(1'b0), .out(Carry_2), .sel(Carry_Block));  // open: en
endmodule

module SETF_CLRF (
  input  [4:0] _8__3_0,
  input  _11,
  output [4:0] Flags
);

  assign Flags[0] = _8__3_0[0] ? ~_11 : 1'bz;  // Controlled_Inverter controlled_inverter_1
  assign Flags[1] = _8__3_0[1] ? ~_11 : 1'bz;  // Controlled_Inverter controlled_inverter_2
  assign Flags[2] = _8__3_0[2] ? ~_11 : 1'bz;  // Controlled_Inverter controlled_inverter_3
  assign Flags[3] = _8__3_0[3] ? ~_11 : 1'bz;  // Controlled_Inverter controlled_inverter_4
  assign Flags[4] = _8__3_0[4] ? ~_11 : 1'bz;  // Controlled_Inverter controlled_inverter_5
endmodule

module MULT (
  input  [15:0] A,
  input  [15:0] B,
  input  [4:0] Flags,
  output [15:0] Product,
  output [15:0] T,
  output [4:0] Flags_2
);

  wire comparator_2_eq;

  Multiplier #(.width(16)) multiplier_1 (.a(A), .b(B), .out(Product), .cout(T));  // open: cin
  Comparator #(.width(16)) comparator_1 (.a(Product), .b({16{1'b0}}), .eq(Flags_2[1]), .lt(Flags_2[0]));  // open: gt
  not not_1 (Flags_2[2], comparator_2_eq);
  Comparator #(.width(16)) comparator_2 (.a(T), .b({16{1'b0}}), .eq(comparator_2_eq));  // open: gt, lt
endmodule

module XOR (
  input  [15:0] A,
  input  [15:0] B,
  input  [4:0] in_3,
  output [15:0] XOR,
  output [4:0] Flags
);

  assign XOR = A ^ B;  // XOR_Gate xor_1, 16 bits wide
  Comparator #(.width(16)) comparator_1 (.a(XOR), .b({16{1'b0}}), .eq(Flags[1]), .lt(Flags[0]));  // open: gt
endmodule

module INC (
  input  [15:0] Rd,
  input  [5:0] Epsilon,
  output [15:0] Rd___e,
  output [4:0] Flags
);

  wire [2:0] undriven;
  wire [4:4] add_1_flags_2;
  wire [15:0] bit_extender_1_out;

  assign bit_extender_1_out = {{10{1'b0}}, Epsilon};  // Bit_Extender bit_extender_1
  ADD add_1 (
    .Input_1(Rd), .Sum(Rd___e), .Input_1_2(bit_extender_1_out), .Flags({2'b01, undriven}),
    .Flags_2({add_1_flags_2[4], Flags[3:0]}));
endmodule

module DEC (
  input  [15:0] Rd,
  input  [5:0] Epsilon,
  output [15:0] Rd___e,
  output [4:0] Flags
);

  wire [2:0] undriven;
  wire [4:4] subtract_1_flags_2;
  wire [15:0] bit_extender_1_out;

  assign bit_extender_1_out = {{10{1'b0}}, Epsilon};  // Bit_Extender bit_extender_1
  SUBTRACT subtract_1 (
    .Ra(Rd), .Ra_Rb__c_F4_prime(Rd___e), .Rb(bit_extender_1_out), .Flags({2'b01, undriven}),
    .Flags_2({subtract_1_flags_2[4], Flags[3:0]}));
endmodule

module SAVEF (
  input  [4:0] Flags,
  output [15:0] Output
);

  assign Output = {{11{1'b0}}, Flags};  // Bit_Extender bit_extender_1
endmodule

module LOAD_STORE (
  input  [15:0] Rb,
  input  [4:0] Offset,
  output [15:0] Rb___o
);

  wire [15:0] bit_extender_1_out;

  assign bit_extender_1_out = {{11{1'b0}}, Offset};  // Bit_Extender bit_extender_1
  Adder #(.width(16)) adder_1 (.a(Rb), .b(bit_extender_1_out), .out(Rb___o));  // open: cin, cout
endmodule

module Flags (
  input  in_1,
  input  CLK,
  input  [4:0] in_3,
  output [4:0] out_4
);

  Register #(.width(1)) Carry_Borrow (.D(in_3[0]), .Q(out_4[0]), .clk(CLK), .clr(in_1));  // open: en
  Register #(.width(1)) Carry_Block (.D(in_3[1]), .Q(out_4[1]), .clk(CLK), .clr(in_1));  // open: en
  Register #(.width(1)) Overflow (.D(1'b0), .Q(out_4[2]), .clk(CLK), .clr(in_1));  // open: en
  Register #(.width(1)) Zero (.D(in_3[3]), .Q(out_4[3]), .clk(CLK), .clr(in_1));  // open: en
  Register #(.width(1)) Sign (.D(1'b1), .Q(out_4[4]), .clk(CLK), .clr(in_1));  // open: en
endmodule

module Registers (
  input  CLK,
  input  [3:0] A,
  input  [3:0] B,
  input  [3:0] D,
  input  [15:0] Data_A,
  input  [15:0] Data_B,
  input  [15:0] Data_D,
  input  [15:0] Data_FP,
  input  [15:0] Data_T,
  input  [15:0] Instruction,
  input  Reset,
  input  [15:0] Keyboard,
  input  [15:0] PC,
  input  [4:0] Flags,
  input  ThreadSwitch,
  input  Privileges,
  output [15:0] A_2,
  output [15:0] B_2,
  output [15:0] D_2,
  output [15:0] R0,
  output [15:0] R1,
  output [15:0] R2,
  output [15:0] R3,
  output [15:0] R4,
  output [15:0] R5,
  output [15:0] R6,
  output [15:0] R7,
  output [15:0] FP,
  output [15:0] Thread_PC,
  output [15:0] R8,
  output [15:0] R9,
  output [15:0] R10,
  output [15:0] R11,
  output [15:0] K1,
  output [4:0] Thread_Flags,
  output [15:0] R12,
  output [15:0] R13,
  output [15:0] R14,
  output [15:0] R15,
  output [15:0] K1_2,
  output New_Flags,
  output R2_2,
  output [15:0] CurrentThread,
  output [15:0] TSLocation,
  output [15:0] StartThread,
  output [15:0] KillThread,
  output [15:0] KillThreadError,
  output [1:0] OS_Select
);

  wire and_1_out, and_2_out, and_3_out, and_4_out, and_5_out, and_6_out, and_7_out, and_8_out,
       comparator_1_eq, comparator_2_eq, comparator_3_eq, comparator_4_eq, comparator_5_eq, comparator_6_eq,
       comparator_7_eq, comparator_8_eq, comparator_9_eq, comparator_10_eq, comparator_11_eq,
       comparator_12_eq, register_25_q;
  wire [15:0] _0, _2, _3, _4, _5, _6, _7, _8, _9, _10, _11, _12, _15, adder_1_out, controlled_buffer_1_out,
       register_19_q, register_20_q, register_21_q, register_22_q, register_23_q, register_24_q;
  wire [15:5] controlled_buffer_3_out, controlled_buffer_7_out, Flags_t;

  Demultiplexer #(.select(4), .width(16), .tristate("true")) demultiplexer_1 (
    .out0(_0), .out1(Keyboard), .out2(_2), .out3(_3), .out4(_4), .out5(_5), .out6(_6), .out7(_7), .out8(_8),
    .out9(_9), .out10(_10), .out11(_11), .out12(_12), .out13(Data_T), .out14(Data_FP), .out15(_15),
    .in(Data_A), .sel(A));  // open: en
  Comparator #(.width(16)) comparator_1 (.a(16'he007), .b(Instruction), .eq(comparator_1_eq));  // open: gt, lt
  Comparator #(.width(16)) comparator_2 (.a(16'he006), .b(Instruction), .eq(comparator_2_eq));  // open: gt, lt
  Comparator #(.width(16)) comparator_3 (.a(16'he006), .b(Instruction), .eq(comparator_3_eq));  // open: gt, lt
  Comparator #(.width(16)) comparator_4 (.a(16'he006), .b(Instruction), .eq(comparator_4_eq));  // open: gt, lt
  Comparator #(.width(16)) comparator_5 (.a(16'he006), .b(Instruction), .eq(comparator_5_eq));  // open: gt, lt
  Register #(.width(16)) register_1 (.D(_0), .en(1'b0), .Q(R0), .clk(CLK), .clr(Reset));
  Register #(.width(16)) register_2 (.D(_4), .Q(R4), .clk(CLK), .clr(Reset));  // open: en
  Register #(.width(16)) register_3 (.D(_8), .Q(R8), .clk(CLK), .clr(Reset));  // open: en
  Register #(.width(16)) register_4 (.D(_12), .Q(R12), .clk(CLK), .clr(Reset));  // open: en
  and and_1 (and_1_out, comparator_1_eq, Privileges);
  and and_2 (and_2_out, comparator_2_eq, Privileges);
  and and_3 (and_3_out, comparator_3_eq, Privileges);
  and and_4 (and_4_out, comparator_4_eq, Privileges);
  and and_5 (and_5_out, comparator_5_eq, Privileges);
  Demultiplexer #(.select(4), .width(16), .tristate("true")) demultiplexer_2 (
    .out0(_0), .out1(Keyboard), .out2(_2), .out3(_3), .out4(_4), .out5(_5), .out6(_6), .out7(_7), .out8(_8),
    .out9(_9), .out10(_10), .out11(_11), .out12(_12), .out13(Data_T), .out14(Data_FP), .out15(_15),
    .in(Data_B), .sel(B));  // open: en
  Register #(.width(16)) register_5 (.D(R1), .en(and_1_out), .Q(CurrentThread), .clk(CLK));  // open: clr
  Register #(.width(16)) register_6 (.D(R1), .en(and_2_out), .Q(TSLocation), .clk(CLK));  // open: clr
  Register #(.width(16)) register_7 (.D(R2), .en(and_3_out), .Q(StartThread), .clk(CLK));  // open: clr
  Register #(.width(16)) register_8 (.D(R3), .en(and_4_out), .Q(KillThread), .clk(CLK));  // open: clr
  Register #(.width(16)) register_9 (.D(R4), .en(and_5_out), .Q(KillThreadError), .clk(CLK));  // open: clr
  Register #(.width(16)) register_10 (.D(Keyboard), .Q(R1), .clk(CLK), .clr(Reset));  // open: en
  Register #(.width(16)) register_11 (.D(_5), .Q(R5), .clk(CLK), .clr(Reset));  // open: en
  Register #(.width(16)) register_12 (.D(_9), .Q(R9), .clk(CLK), .clr(Reset));  // open: en
  Register #(.width(16)) Temp (.D(Data_T), .Q(R13), .clk(CLK), .clr(Reset));  // open: en
  Register #(.width(16)) register_13 (.D(_2), .Q(R2), .clk(CLK), .clr(Reset));  // open: en
  Register #(.width(16)) register_14 (.D(_6), .Q(R6), .clk(CLK), .clr(Reset));  // open: en
  Register #(.width(16)) register_15 (.D(_10), .Q(R10), .clk(CLK), .clr(Reset));  // open: en
  Register #(.width(16)) u_FP (.D(Data_FP), .Q(FP), .clk(CLK), .clr(Reset));  // open: en
  Multiplexer #(.select(2), .width(2)) multiplexer_1 (
    .in1(2'b00), .in2(2'b01), .in3(2'b10), .out(OS_Select), .sel(R1[1:0]), .en(comparator_6_eq));  // open: in0
  Comparator #(.width(16)) comparator_6 (.a(16'he008), .b(Instruction), .eq(comparator_6_eq));  // open: gt, lt
  Register #(.width(16)) register_16 (.D(_3), .Q(R3), .clk(CLK), .clr(Reset));  // open: en
  Register #(.width(16)) register_17 (.D(_7), .Q(R7), .clk(CLK), .clr(Reset));  // open: en
  Register #(.width(16)) register_18 (.D(_11), .Q(R11), .clk(CLK), .clr(Reset));  // open: en
  Register #(.width(16)) SP (.D(_15), .Q(R15), .clk(CLK), .clr(Reset));  // open: en
  Demultiplexer #(.select(4), .width(16), .tristate("true")) demultiplexer_3 (
    .out0(_0), .out1(Keyboard), .out2(_2), .out3(_3), .out4(_4), .out5(_5), .out6(_6), .out7(_7), .out8(_8),
    .out9(_9), .out10(_10), .out11(_11), .out12(_12), .out13(Data_T), .out14(Data_FP), .out15(_15),
    .in(Data_D), .sel(D));  // open: en
  Comparator #(.width(16)) comparator_7 (.a(16'he001), .b(Instruction), .eq(comparator_7_eq));  // open: gt, lt
  Comparator #(.width(16)) comparator_8 (.a(16'he008), .b(Instruction), .eq(comparator_8_eq));  // open: gt, lt
  and and_6 (and_6_out, comparator_7_eq, Privileges);
  Adder #(.width(16)) adder_1 (.a(PC), .b(16'h1), .out(adder_1_out));  // open: cin, cout
  Register #(.width(16)) register_19 (.D(R10), .en(and_6_out), .Q(register_19_q), .clk(CLK));  // open: clr
  Register #(.width(16)) register_20 (.D(R11), .en(and_6_out), .Q(register_20_q), .clk(CLK));  // open: clr
  Register #(.width(16)) register_21 (.D(PC), .en(ThreadSwitch), .Q(register_21_q), .clk(CLK));  // open: clr
  Register #(.width(16)) register_22 (
    .D({Flags_t, Flags}), .en(ThreadSwitch), .Q(register_22_q), .clk(CLK));  // open: clr
  Register #(.width(16)) register_23 (
    .D(adder_1_out), .en(comparator_8_eq), .Q(register_23_q), .clk(CLK));  // open: clr
  Register #(.width(16)) register_24 (
    .D({Flags_t, Flags}), .en(comparator_8_eq), .Q(register_24_q), .clk(CLK));  // open: clr
  Register #(.width(1)) register_25 (.D(Privileges), .en(comparator_8_eq), .Q(register_25_q), .clk(CLK));  // open: clr
  Comparator #(.width(16)) comparator_9 (.a(16'he002), .b(Instruction), .eq(comparator_9_eq));  // open: gt, lt
  Comparator #(.width(16)) comparator_10 (.a(16'he000), .b(Instruction), .eq(comparator_10_eq));  // open: gt, lt
  Comparator #(.width(16)) comparator_11 (.a(16'he009), .b(Instruction), .eq(comparator_11_eq));  // open: gt, lt
  assign controlled_buffer_1_out = comparator_12_eq ? R1 : 16'bz;  // Controlled_Buffer controlled_buffer_1
  Comparator comparator_12 (.a(8'h11), .b(Instruction[15:8]), .eq(comparator_12_eq));  // open: gt, lt
  assign Thread_PC = comparator_9_eq ? register_19_q : 16'bz;  // Controlled_Buffer controlled_buffer_2
  assign {controlled_buffer_3_out, Thread_Flags} = comparator_9_eq ? register_20_q : 16'bz;  // Controlled_Buffer controlled_buffer_3
  assign _10 = and_7_out ? register_21_q : 16'bz;  // Controlled_Buffer controlled_buffer_4
  and and_7 (and_7_out, comparator_10_eq, Privileges);
  assign _11 = and_7_out ? register_22_q : 16'bz;  // Controlled_Buffer controlled_buffer_5
  assign Thread_PC = and_8_out ? register_23_q : 16'bz;  // Controlled_Buffer controlled_buffer_6
  and and_8 (and_8_out, comparator_11_eq, Privileges);
  assign {controlled_buffer_7_out, Thread_Flags} = and_8_out ? register_24_q : 16'bz;  // Controlled_Buffer controlled_buffer_7
  assign New_Flags = and_8_out ? register_25_q : 1'bz;  // Controlled_Buffer controlled_buffer_8
  Multiplexer #(.select(4), .width(16), .enable("false")) multiplexer_2 (
    .in0(R0), .in1(R1), .in2(R2), .in3(R3), .in4(R4), .in5(R5), .in6(R6), .in7(R7), .in8(R8), .in9(R9),
    .in10(R10), .in11(R11), .in12(R12), .in13(R13), .in14(FP), .in15(R15), .out(A_2), .sel(A));
  Multiplexer #(.select(4), .width(16), .enable("false")) multiplexer_3 (
    .in0(R0), .in1(R1), .in2(R2), .in3(R3), .in4(R4), .in5(R5), .in6(R6), .in7(R7), .in8(R8), .in9(R9),
    .in10(R10), .in11(R11), .in12(R12), .in13(R13), .in14(FP), .in15(R15), .out(B_2), .sel(B));
  Multiplexer #(.select(4), .width(16), .enable("false")) multiplexer_4 (
    .in0(R0), .in1(R1), .in2(R2), .in3(R3), .in4(R4), .in5(R5), .in6(R6), .in7(R7), .in8(R8), .in9(R9),
    .in10(R10), .in11(R11), .in12(R12), .in13(R13), .in14(FP), .in15(R15), .out(D_2), .sel(D));
  Demultiplexer #(.width(16), .tristate("true"), .enable("false")) demultiplexer_4 (
    .out0(K1), .out1(K1_2), .in(controlled_buffer_1_out), .sel(R2[0]));

  assign R2_2 = R2[0];
  assign R14 = FP;

  // Other names for the same wires on the sheet: OS_Thread_Flags[4:0] = Thread_Flags; _1[15:0] = Keyboard;
  //   _13[15:0] = Data_T; _14[15:0] = Data_FP; Flags_t[4:0] = Flags; OS_Thread_PC[15:0] = Thread_PC;
  //   PrivilegesOut = New_Flags
endmodule

module OR (
  input  [15:0] A,
  input  [15:0] B,
  input  [4:0] in_3,
  output [15:0] XOR,
  output [4:0] Flags
);

  assign XOR = A | B;  // OR_Gate or_1, 16 bits wide
  Comparator #(.width(16)) comparator_1 (.a(XOR), .b({16{1'b0}}), .eq(Flags[1]), .lt(Flags[0]));  // open: gt
endmodule

module CALL_RETURN_Interrupt (
  input  [15:0] PC,
  input  [15:0] Ra,
  input  [15:0] Rb,
  input  [15:0] FP,
  input  [3:0] Opcode,
  input  [3:0] Instruction,
  input  [3:0] Interrupt,
  output [15:0] PC_2,
  output [15:0] Ra_2,
  output [15:0] Rb_2,
  output [15:0] Fp_2
);

  wire comparator_1_eq, comparator_2_eq;
  wire [15:0] adder_1_out, controlled_buffer_4_out, Interrupt_Location;

  Comparator #(.width(4), .mode("unsigned")) comparator_1 (
    .a(Opcode), .b(4'b0010), .eq(comparator_1_eq));  // open: gt, lt
  assign PC_2 = comparator_1_eq ? Interrupt_Location : 16'bz;  // Controlled_Buffer controlled_buffer_1
  assign Ra_2 = comparator_1_eq ? FP : 16'bz;  // Controlled_Buffer controlled_buffer_2
  assign Rb_2 = comparator_2_eq ? controlled_buffer_4_out : 16'bz;  // Controlled_Buffer controlled_buffer_3
  assign controlled_buffer_4_out = comparator_1_eq ? adder_1_out : 16'bz;  // Controlled_Buffer controlled_buffer_4
  Adder #(.width(16)) adder_1 (.a(PC), .b(16'h1), .out(adder_1_out));  // open: cin, cout
  assign Fp_2 = comparator_1_eq ? Ra : 16'bz;  // Controlled_Buffer controlled_buffer_5
  Comparator #(.width(4), .mode("unsigned")) comparator_2 (
    .a(Instruction), .b(4'b0000), .eq(comparator_2_eq));  // open: gt, lt
endmodule

module Control_Flow (
  input  CLK,
  input  [3:0] _15_12,
  input  [3:0] _11_8,
  input  [7:0] _7_0,
  input  Reset,
  input  [15:0] B,
  input  [4:0] Flags,
  input  [15:0] I,
  input  Keystroke,
  input  [15:0] Thread_PC,
  input  ThreadSwitch,
  input  [15:0] ThreadService,
  input  [15:0] StartThread,
  input  [15:0] KillThread,
  input  [1:0] OS_Select,
  input  [15:0] KillThreadError,
  input  ThreadError,
  input  Privileges,
  output [15:0] Address
);

  wire Branch_Condition, comparator_1_eq, comparator_2_eq, Condition, Interrupt_t, Load_New_PC,
       multiplexer_5_out, not_1_out, not_2_out, OS_Op, OS_Thing, Return, ThreadSwitch_t, TS_Thing;
  wire [2:0] New_PC;
  wire [15:0] Branch_Counter, C_R_Location, Counter, Interrupt_PC, multiplexer_4_out, multiplexer_6_out;

  Multiplexer #(.select(4)) multiplexer_1 (
    .in0(Branch_Condition), .in1(Branch_Condition), .in2(1'b1), .in3(1'b0), .in4(1'b0), .in5(1'b0),
    .in6(1'b0), .in7(1'b0), .in8(1'b0), .in9(1'b0), .in10(1'b0), .in11(1'b0), .in12(1'b0), .in13(1'b0),
    .in14(1'b0), .in15(1'b0), .out(Condition), .sel(_15_12));  // open: en
  Multiplexer #(.select(4), .width(16)) multiplexer_2 (
    .in0(B), .in1(B), .in2(I), .in3(I), .out(C_R_Location), .sel(_11_8));  // open: in4, in5, in6, in7, in8, in9, in10, in11, in12, in13, in14, in15, en
  Branch Branch (
    .CLK(CLK), ._15_12(_15_12), ._11_8(_11_8), ._7_0(_7_0), .B(B), .Address(Address), .Flags(Flags),
    .Condition(Branch_Condition), .Counter(Branch_Counter));
  Comparator #(.width(16)) comparator_1 (
    .a(16'he009), .b({_15_12, _11_8, _7_0}), .eq(comparator_1_eq));  // open: gt, lt
  Comparator #(.width(16)) comparator_2 (
    .a(16'he002), .b({_15_12, _11_8, _7_0}), .eq(comparator_2_eq));  // open: gt, lt
  Multiplexer #(.select(4), .width(16)) multiplexer_3 (
    .in0(Branch_Counter), .in1(Branch_Counter), .in2(C_R_Location), .in3({16{1'b0}}), .in4({16{1'b0}}),
    .in5({16{1'b0}}), .in6({16{1'b0}}), .in7({16{1'b0}}), .in8({16{1'b0}}), .in9({16{1'b0}}),
    .in10({16{1'b0}}), .in11({16{1'b0}}), .in12({16{1'b0}}), .in13({16{1'b0}}), .in14({16{1'b0}}),
    .in15({16{1'b0}}), .out(Counter), .sel(_15_12));  // open: en
  Interrupt Interrupt (
    .PC(Address), .Opcode(_15_12), .Instruction(_11_8), .Interrupt(_7_0[3:0]), .CLK(CLK),
    .PC_2(Interrupt_PC), .Keystroke(Keystroke));
  and and_1 (OS_Thing, comparator_1_eq, Privileges);
  and and_2 (TS_Thing, comparator_2_eq, Privileges);
  D_Flip_Flop d_ff_1 (.clk(CLK));  // open: D, Q, Qn, preset, en, reset
  Multiplexer #(.select(2), .width(16)) multiplexer_4 (
    .in0(StartThread), .in1(KillThread), .out(multiplexer_4_out), .sel(OS_Select));  // open: in2, in3, en
  Comparator comparator_3 (.a({_15_12, _11_8}), .b(8'h22), .eq(Interrupt_t));  // open: gt, lt
  assign New_PC = Interrupt_t ? 3'b001 : 3'bz;  // Controlled_Buffer controlled_buffer_1
  Comparator comparator_4 (.a({_15_12, _11_8}), .b(8'h23), .eq(Return));  // open: gt, lt
  or or_1 (ThreadSwitch_t, OS_Thing, TS_Thing);
  assign New_PC = ThreadSwitch_t ? 3'b010 : 3'bz;  // Controlled_Buffer controlled_buffer_2
  assign New_PC = ThreadSwitch ? 3'b011 : 3'bz;  // Controlled_Buffer controlled_buffer_3
  Comparator #(.width(16)) comparator_5 (.a(16'he008), .b({_15_12, _11_8, _7_0}), .eq(OS_Op));  // open: gt, lt
  assign New_PC = ThreadError ? 3'b101 : 3'bz;  // Controlled_Buffer controlled_buffer_4
  assign New_PC = OS_Op ? 3'b100 : 3'bz;  // Controlled_Buffer controlled_buffer_5
  Multiplexer multiplexer_5 (.in0(Condition), .in1(1'b1), .out(multiplexer_5_out), .sel(Load_New_PC));  // open: en
  // Probe on multiplexer_6_out
  Multiplexer #(.select(3), .width(16)) multiplexer_6 (
    .in0(Counter), .in1(Interrupt_PC), .in2(Thread_PC), .in3(ThreadService), .in4(multiplexer_4_out),
    .in5(KillThreadError), .out(multiplexer_6_out), .sel(New_PC));  // open: in6, in7, en
  // Probe on New_PC
  or or_2 (Load_New_PC, ThreadError, ThreadSwitch, Keystroke, Interrupt_t, Return, ThreadSwitch_t, OS_Op, OS_Thing);
  not not_1 (not_1_out, multiplexer_5_out);
  not not_2 (not_2_out, Load_New_PC);
  assign New_PC = not_2_out ? 3'b000 : 3'bz;  // Controlled_Buffer controlled_buffer_6
  Counter #(.width(16), .max('hffff)) counter_1 (
    .load(multiplexer_5_out), .D(multiplexer_6_out), .count(not_1_out), .Q(Address), .clk(CLK), .clr(Reset));  // open: carry

  // Other names for the same wires on the sheet: c[3:0] = _11_8; Instructions[15:0] = {_15_12, _11_8, _7_0};
  //   Opcode[3:0] = _15_12; Interrupt[3:0] = _7_0[3:0]; Offset[7:0] = _7_0; Interrupt_Location[15:0] = I;
  //   OS_Thread_PC[15:0] = Thread_PC; ThreadHappened = ThreadSwitch
endmodule

module Branch (
  input  CLK,
  input  [3:0] _15_12,
  input  [3:0] _11_8,
  input  [7:0] _7_0,
  input  [15:0] B,
  input  [15:0] Address,
  input  [4:0] Flags,
  output Condition,
  output [15:0] Counter
);

  wire BG_BGR, BGE_BGER, BL_BLR, BLE_BLER, BNC_BNCR, BNS_BNSR, BNV_BNVR, BNZ_BNZR, BUG_BUGR, BULE_BULER,
       not_1_out, not_9_out;
  wire [15:0] adder_1_out, bit_extender_1_out;

  assign bit_extender_1_out = {{8{1'b0}}, _7_0};  // Bit_Extender bit_extender_1
  xor xor_1 (BL_BLR, Flags[0], Flags[2]);
  not not_1 (not_1_out, Flags[3]);
  Adder #(.width(16)) adder_1 (.a(bit_extender_1_out), .b(Address), .out(adder_1_out));  // open: cin, cout
  not not_2 (BGE_BGER, BL_BLR);
  or or_1 (BLE_BLER, BL_BLR, Flags[1]);
  not not_3 (BG_BGR, BLE_BLER);
  or or_2 (BULE_BULER, Flags[1], not_1_out);
  not not_4 (BUG_BUGR, BULE_BULER);
  not not_5 (BNZ_BNZR, Flags[1]);
  not not_6 (BNC_BNCR, Flags[3]);
  not not_7 (BNS_BNSR, Flags[0]);
  not not_8 (BNV_BNVR, Flags[2]);
  Multiplexer #(.width(16), .enable("false")) multiplexer_1 (
    .in0(B), .in1(adder_1_out), .out(Counter), .sel(not_9_out));
  not not_9 (not_9_out, _15_12[0]);
  Multiplexer #(.select(4)) multiplexer_2 (
    .in0(1'b1), .in2(BL_BLR), .in3(BGE_BGER), .in4(BLE_BLER), .in5(BG_BGR), .in6(BULE_BULER), .in7(BUG_BUGR),
    .in8(Flags[1]), .in9(BNZ_BNZR), .in10(Flags[3]), .in11(BNC_BNCR), .in12(Flags[0]), .in13(BNS_BNSR),
    .in14(Flags[2]), .in15(BNV_BNVR), .out(Condition), .sel(_11_8));  // open: in1, en

  // Other names for the same wires on the sheet: Register = _15_12[0]; c[3:0] = _11_8; BS_BSR = Flags[0];
  //   Sign = Flags[0]; BZ_BZR = Flags[1]; Zero = Flags[1]; BV_BVR = Flags[2]; Overflow = Flags[2]; BC_BCR = Flags[3];
  //   Carry = Flags[3]; Carry_Block = Flags[4]; Offset[7:0] = _7_0
endmodule

module Flag (
  input  [4:0] in_1,
  output out_2,
  output out_3,
  output out_4,
  output out_5,
  output out_6
);


  assign out_2 = in_1[0];
  assign out_3 = in_1[1];
  assign out_4 = in_1[2];
  assign out_5 = in_1[3];
  assign out_6 = in_1[4];
endmodule

module Interrupt (
  input  [15:0] PC,
  input  [3:0] Opcode,
  input  [3:0] Instruction,
  input  [3:0] Interrupt,
  input  CLK,
  input  Keystroke,
  output [15:0] PC_2
);

  wire Interrupt_t, or_1_out, or_2_out, or_3_out, Return;
  wire [15:0] multiplexer_1_out, Stored_PC;

  or or_1 (or_1_out, Keystroke, Interrupt_t);
  Register #(.width(16)) register_1 (.D(PC), .en(or_1_out), .Q(Stored_PC), .clk(CLK));  // open: clr
  // Probe on Stored_PC
  Comparator comparator_1 (.a({Opcode, Instruction}), .b(8'h22), .eq(Interrupt_t));  // open: gt, lt
  Comparator comparator_2 (.a({Opcode, Instruction}), .b(8'h23), .eq(Return));  // open: gt, lt
  Multiplexer #(.width(16)) multiplexer_1 (
    .in0(Stored_PC), .in1(16'h13), .out(multiplexer_1_out), .sel(or_2_out));  // open: en
  or or_2 (or_2_out, Keystroke, Interrupt_t);
  or or_3 (or_3_out, Keystroke, Interrupt_t, Return);
  assign PC_2 = or_3_out ? multiplexer_1_out : 16'bz;  // Controlled_Buffer controlled_buffer_1
endmodule

module putchar (
  input  [15:0] Opcode,
  input  CLK
);

  wire put_char;
  wire [6:0] Monitor_1, Monitor_2;

  TTY tty_1 (.data(Monitor_1), .clk(CLK));  // open: we, clr
  Comparator comparator_1 (.a(Opcode[15:8]), .b(8'h44), .eq(put_char));  // open: gt, lt
  Demultiplexer #(.width(7)) demultiplexer_1 (
    .out0(Monitor_1), .out1(Monitor_2), .in(Opcode[6:0]), .sel(Opcode[7]), .en(put_char));
  TTY tty_2 (.data(Monitor_2), .clk(CLK));  // open: we, clr

  // Other names for the same wires on the sheet: Data[6:0] = Opcode[6:0]; Monitor = Opcode[7];
  //   Opcode_t[7:0] = Opcode[15:8]
endmodule

module getchar (
  input  [15:0] Opcode,
  input  CLK,
  input  in_3,
  output [6:0] Ascii,
  output out_5
);

  wire getchar, K1R, K2R, not_1_out;
  wire [6:0] K1, K2;

  Keyboard keyboard_1 (.clk(CLK), .re(Opcode[7]), .avail(K1R), .data(K1));  // open: clr
  Keyboard keyboard_2 (.clk(CLK), .re(not_1_out), .avail(K2R), .data(K2));  // open: clr
  not not_1 (not_1_out, Opcode[7]);
  Comparator comparator_1 (.a(Opcode[15:8]), .b(8'h45), .eq(getchar));  // open: gt, lt
  Multiplexer #(.width(7)) multiplexer_1 (.in0(K1), .in1(K2), .out(Ascii), .sel(Opcode[7]), .en(in_3));
  Multiplexer multiplexer_2 (.in0(K1R), .in1(K2R), .out(out_5), .sel(Opcode[7]));  // open: en

  // Other names for the same wires on the sheet: Keyboard = Opcode[7]; _8_15[7:0] = Opcode[15:8]
endmodule

module KeyboardMemoryStore (
  input  [15:0] Instructions,
  input  [15:0] CT,
  input  [15:0] Address,
  input  [15:0] Data,
  input  Privileges,
  input  K1_Input,
  input  K2_Input,
  input  store,
  input  select,
  input  CLK,
  input  load,
  input  clr,
  output [15:0] New_Address,
  output [15:0] New_Data,
  output store_2,
  output select_2,
  output CLK_2,
  output load_2,
  output clr_2,
  output ThreadError
);

  wire and_2_out, and_3_out, Both_Input, d_ff_1_q, d_ff_2_q, Input, K1_New, K2_New, Keyboard_Empty,
       Keyboard_Input, not_1_out, not_2_out, not_3_out, not_4_out, or_2_out, or_3_out, or_4_out, or_5_out,
       or_6_out, or_7_out, OS_Code, PublicOS, ThreadAllow, ThreadMemory, WithinOS, xor_1_out, xor_2_out;
  wire [15:0] multiplexer_1_out, multiplexer_2_out, multiplexer_3_out, multiplexer_4_out, NewAddress;

  or or_1 (Input, K1_Input, K2_Input);
  and and_1 (Both_Input, K1_Input, K2_Input);
  New_Keyboard_Input new_keyboard_input_1 (
    .CLK(CLK), .clr(clr), .K1_Input(K1_Input), .K2_Input(K2_Input), .New_Keyboard_Input(Keyboard_Input),
    .Keyboard_Empty(Keyboard_Empty));  // open: New_Interrupt, Opcode, Instruction
  D_Flip_Flop d_ff_1 (.clk(CLK), .D(K1_New), .Q(d_ff_1_q), .reset(clr));  // open: Qn, preset, en
  D_Flip_Flop d_ff_2 (.clk(CLK), .D(K2_New), .Q(d_ff_2_q), .reset(clr));  // open: Qn, preset, en
  xor xor_1 (xor_1_out, d_ff_1_q, K1_Input);
  xor xor_2 (xor_2_out, d_ff_2_q, K2_Input);
  MMU mmu_1 (
    .Instructions(Instructions), .CT(CT), .Address(Address), .Load(load), .Store(store),
    .New_Address(NewAddress), .ThreadAllow(ThreadAllow), .WithinOS(WithinOS), .PublicOS(PublicOS),
    .ThreadError(ThreadError), .ThreadMemory(ThreadMemory), .Load_Store(select));
  Comparator #(.width(16)) comparator_1 (.a(16'he008), .b(Instructions), .eq(OS_Code));  // open: gt, lt
  and and_2 (and_2_out, xor_1_out, xor_2_out);
  or or_2 (or_2_out, xor_1_out, and_2_out, xor_2_out);
  and and_3 (and_3_out, ThreadMemory, ThreadAllow);
  or or_3 (or_3_out, and_3_out, ~Privileges);  // OR_Gate
  Multiplexer #(.width(16)) multiplexer_1 (
    .in0(Address), .in1(NewAddress), .out(multiplexer_1_out), .sel(or_3_out), .en(not_1_out));
  not not_1 (not_1_out, ThreadError);
  Multiplexer #(.width(16), .enable("false")) multiplexer_2 (
    .in0(16'h1), .in1(16'h2), .out(multiplexer_2_out), .sel(K2_Input));
  Multiplexer #(.width(16), .enable("false")) multiplexer_3 (
    .in0(Data), .in1({16{1'b0}}), .out(multiplexer_3_out), .sel(Keyboard_Empty));
  Multiplexer #(.width(16), .enable("false")) multiplexer_4 (
    .in0(multiplexer_2_out), .in1(16'h3), .out(multiplexer_4_out), .sel(Both_Input));
  Multiplexer #(.width(16), .enable("false")) multiplexer_5 (
    .in0(multiplexer_1_out), .in1(16'h4000), .out(New_Address), .sel(or_4_out));
  or or_4 (or_4_out, Keyboard_Input, Keyboard_Empty);
  Multiplexer #(.width(16), .enable("false")) multiplexer_6 (
    .in0(multiplexer_3_out), .in1(multiplexer_4_out), .out(New_Data), .sel(Keyboard_Input));
  Multiplexer #(.disabled(0)) multiplexer_7 (.in0(store), .in1(1'b1), .out(store_2), .sel(or_5_out), .en(not_2_out));
  not not_2 (not_2_out, ThreadError);
  or or_5 (or_5_out, Keyboard_Input, Keyboard_Empty);
  Multiplexer #(.disabled(0)) multiplexer_8 (.in0(select), .in1(1'b1), .out(select_2), .sel(or_6_out), .en(not_3_out));
  not not_3 (not_3_out, ThreadError);
  or or_6 (or_6_out, Keyboard_Input, Keyboard_Empty);
  Multiplexer #(.disabled(0)) multiplexer_9 (.in0(load), .in1(1'b0), .out(load_2), .sel(or_7_out), .en(not_4_out));
  not not_4 (not_4_out, ThreadError);
  or or_7 (or_7_out, Keyboard_Input, Keyboard_Empty);

  assign CLK_2 = CLK;
  assign clr_2 = clr;

  // Other names for the same wires on the sheet: KeyboardMemoryClr = Keyboard_Empty; New_load = load_2;
  //   New_select = select_2; New_store = store_2
endmodule

module LOAD_Flags (
  input  [15:0] in_1,
  input  [3:0] in_2,
  output [4:0] out_3
);

  wire comparator_2_eq, comparator_2_lt, isLoad;

  Comparator #(.width(3)) comparator_1 (.a(in_2[3:1]), .b(3'b010), .eq(isLoad));  // open: gt, lt
  Comparator #(.width(16)) comparator_2 (
    .a(in_1), .b({16{1'b0}}), .eq(comparator_2_eq), .lt(comparator_2_lt));  // open: gt
  assign out_3[1] = isLoad ? comparator_2_eq : 1'bz;  // Controlled_Buffer controlled_buffer_1
  assign out_3[0] = isLoad ? comparator_2_lt : 1'bz;  // Controlled_Buffer controlled_buffer_2
endmodule

module New_Keyboard_Input (
  input  CLK,
  input  clr,
  input  K1_Input,
  input  K2_Input,
  input  [3:0] Opcode,
  input  [3:0] Instruction,
  output New_Keyboard_Input,
  output Keyboard_Empty,
  output New_Interrupt
);

  wire and_1_out, and_2_out, d_ff_3_q, K1_Old, K2_Old, nand_1_out, nand_2_out, nand_3_out, nor_1_out,
       not_1_out, or_1_out, or_2_out, or_3_out, or_4_out, or_6_out, register_1_q, Return;

  Comparator comparator_1 (.a({Opcode, Instruction}), .b(8'h23), .eq(Return));  // open: gt, lt
  or or_1 (or_1_out, K1_Input, K2_Input);
  or or_2 (or_2_out, clr, Return);
  D_Flip_Flop d_ff_1 (.clk(CLK), .D(K1_Input), .Q(K1_Old), .reset(clr));  // open: Qn, preset, en
  D_Flip_Flop d_ff_2 (.clk(CLK), .D(K2_Input), .Q(K2_Old), .reset(clr));  // open: Qn, preset, en
  D_Flip_Flop d_ff_3 (.clk(CLK), .D(or_1_out), .Q(d_ff_3_q), .en(not_1_out), .reset(or_2_out));  // open: Qn, preset
  not not_1 (not_1_out, d_ff_3_q);
  nand nand_1 (nand_1_out, K1_Old, K1_Input);
  nand nand_2 (nand_2_out, K2_Old, K2_Input);
  and and_1 (and_1_out, K1_Input, nand_1_out);
  and and_2 (and_2_out, nand_2_out, K2_Input);
  or or_3 (or_3_out, K1_Old, K2_Old);
  nand nand_3 (nand_3_out, d_ff_3_q, or_4_out);
  or or_4 (or_4_out, K1_Input, K2_Input);
  or or_5 (New_Keyboard_Input, and_1_out, and_2_out);
  Register #(.width(1)) register_1 (.D(or_3_out), .Q(register_1_q), .clk(CLK), .clr(clr));  // open: en
  nor nor_1 (nor_1_out, K1_Input, K2_Input);
  and and_3 (Keyboard_Empty, register_1_q, nor_1_out);
  and and_4 (New_Interrupt, nand_3_out, or_6_out);
  or or_6 (or_6_out, K1_Input, K2_Input);
endmodule

module LSL8 (
  input  [15:0] Rd,
  input  [4:0] Flags,
  output [15:0] shr_rolc_Rd,
  output [4:0] Flags_2
);

  Comparator #(.width(16)) comparator_1 (
    .a({{8{1'b0}}, Rd[15:8]}), .b({16{1'b0}}), .eq(Flags_2[1]), .lt(Flags_2[0]));  // open: gt

  assign shr_rolc_Rd = {{8{1'b0}}, Rd[15:8]};
endmodule

module LSR8 (
  input  [15:0] Rd,
  input  [4:0] Flags,
  output [15:0] shr_rolc_Rd,
  output [4:0] Flags_2
);

  Comparator #(.width(16)) comparator_1 (
    .a({Rd[7:0], {8{1'b0}}}), .b({16{1'b0}}), .eq(Flags_2[1]), .lt(Flags_2[0]));  // open: gt

  assign shr_rolc_Rd = {Rd[7:0], {8{1'b0}}};
endmodule

module RSTRF (
  input  [15:0] Rd,
  output [4:0] New_Flags
);


  assign New_Flags = Rd[4:0];
endmodule

module CPU (
);

  wire [4:0] ALSU_Flags, Flags;
  wire [15:0] A, ALSU_Out, B, D, Data_T, Instruction;

  ALSU alsu_1 (
    .A(A), .B(B), .D(D), .Instruction(Instruction), .Flags(Flags), .Data(ALSU_Out), .Flags_2(ALSU_Flags),
    .T(Data_T));
endmodule

module ThreadControl (
  input  [15:0] Instruction,
  input  CLK,
  input  in_3,
  output ThreadSwitch
);

  wire and_1_out, and_2_out, comparator_1_eq, comparator_2_eq, comparator_3_eq, comparator_4_eq,
       controlled_buffer_1_out, d_ff_1_qn, d_ff_2_qn, d_ff_3_q, multiplexer_1_out, multiplexer_2_out,
       not_1_out, not_2_out, or_1_out;
  wire [7:0] counter_1_q;

  Comparator #(.width(16)) comparator_1 (.a(16'he004), .b(Instruction), .eq(comparator_1_eq));  // open: gt, lt
  Comparator #(.width(16)) comparator_2 (.a(16'he005), .b(Instruction), .eq(comparator_2_eq));  // open: gt, lt
  Comparator #(.width(16)) comparator_3 (.a(16'he002), .b(Instruction), .eq(comparator_3_eq));  // open: gt, lt
  and and_1 (and_1_out, comparator_1_eq, in_3);
  and and_2 (and_2_out, comparator_2_eq, in_3);
  D_Flip_Flop d_ff_1 (.clk(CLK), .D(and_1_out), .Qn(d_ff_1_qn), .en(and_1_out));  // open: Q, preset, reset
  D_Flip_Flop d_ff_2 (.clk(CLK), .D(multiplexer_1_out), .Qn(d_ff_2_qn), .en(or_1_out));  // open: Q, preset, reset
  Multiplexer multiplexer_1 (.in0(1'b1), .in1(1'b0), .out(multiplexer_1_out), .sel(comparator_3_eq));  // open: en
  or or_1 (or_1_out, comparator_3_eq, ThreadSwitch);
  D_Flip_Flop d_ff_3 (.clk(CLK), .D(and_2_out), .Q(d_ff_3_q), .en(and_2_out), .reset(and_1_out));  // open: Qn, preset
  Counter counter_1 (
    .count(d_ff_2_qn), .Q(counter_1_q), .clk(controlled_buffer_1_out), .clr(ThreadSwitch));  // open: load, D, carry
  assign controlled_buffer_1_out = not_1_out ? CLK : 1'bz;  // Controlled_Buffer controlled_buffer_1
  not not_1 (not_1_out, multiplexer_2_out);
  Multiplexer multiplexer_2 (.in0(d_ff_1_qn), .in1(1'b1), .out(multiplexer_2_out), .sel(d_ff_3_q));  // open: en
  Comparator comparator_4 (.a(8'h64), .b(counter_1_q), .eq(comparator_4_eq));  // open: gt, lt
  D_Flip_Flop d_ff_4 (.clk(CLK), .D(comparator_4_eq), .Q(ThreadSwitch), .en(not_2_out));  // open: Qn, preset, reset
  not not_2 (not_2_out, in_3);

  // Other names for the same wires on the sheet: Privileges = in_3
endmodule

module MMU (
  input  [15:0] Instructions,
  input  [15:0] CT,
  input  [15:0] Address,
  input  Load,
  input  Store,
  input  Load_Store,
  output [15:0] New_Address,
  output ThreadAllow,
  output WithinOS,
  output PublicOS,
  output ThreadError,
  output ThreadMemory
);

  wire and_2_out, comparator_1_eq, comparator_1_lt, comparator_2_eq, comparator_2_gt, comparator_3_eq,
       comparator_3_lt, comparator_4_eq, comparator_4_gt, comparator_5_eq, comparator_5_lt, comparator_6_eq,
       comparator_6_gt, or_1_out, or_2_out, or_3_out, or_4_out, or_5_out, or_6_out;
  wire [15:0] MaxAddress, MinAddress, multiplier_1_out;

  Multiplier #(.width(16)) multiplier_1 (.a(CT), .b(16'h64), .out(multiplier_1_out));  // open: cin, cout
  Adder #(.width(16)) adder_1 (.a(Address), .b(MinAddress), .out(New_Address));  // open: cin, cout
  Comparator #(.width(16)) comparator_1 (
    .a(New_Address), .b(16'hfa0), .eq(comparator_1_eq), .lt(comparator_1_lt));  // open: gt
  Comparator #(.width(16)) comparator_2 (
    .a(New_Address), .b(16'h3e8), .gt(comparator_2_gt), .eq(comparator_2_eq));  // open: lt
  Adder #(.width(16)) adder_2 (.a(multiplier_1_out), .b(16'h3e8), .out(MinAddress));  // open: cin, cout
  Comparator #(.width(16)) comparator_3 (
    .a(New_Address), .b(MaxAddress), .eq(comparator_3_eq), .lt(comparator_3_lt));  // open: gt
  or or_1 (or_1_out, comparator_3_eq, comparator_3_lt);
  or or_2 (or_2_out, comparator_4_gt, comparator_4_eq);
  Comparator #(.width(16)) comparator_4 (
    .a(New_Address), .b(MinAddress), .gt(comparator_4_gt), .eq(comparator_4_eq));  // open: lt
  Comparator #(.width(16)) comparator_5 (
    .a(Address), .b(16'h1388), .eq(comparator_5_eq), .lt(comparator_5_lt));  // open: gt
  or or_3 (or_3_out, comparator_5_eq, comparator_5_lt);
  Comparator #(.width(16)) comparator_6 (
    .a(Address), .b(16'hfa0), .gt(comparator_6_gt), .eq(comparator_6_eq));  // open: lt
  or or_4 (or_4_out, comparator_6_gt, comparator_6_eq);
  Comparator #(.width(16)) comparator_7 (.a(Address), .b(16'h1388), .gt(PublicOS));  // open: eq, lt
  or or_5 (or_5_out, comparator_1_eq, comparator_1_lt);
  or or_6 (or_6_out, comparator_2_gt, comparator_2_eq);
  and and_1 (ThreadError, ~ThreadAllow, and_2_out);  // AND_Gate
  and and_2 (and_2_out, ThreadMemory, Load_Store);
  Adder #(.width(16)) adder_3 (.a(MinAddress), .b(16'h64), .out(MaxAddress));  // open: cin, cout
  and and_3 (ThreadAllow, or_1_out, or_2_out);
  and and_4 (WithinOS, or_3_out, or_4_out);
  and and_5 (ThreadMemory, or_5_out, or_6_out);

  // Other names for the same wires on the sheet: Instruction[15:0] = Instructions; L_S_Check = Load_Store;
  //   NewAddress[15:0] = New_Address; PublicMemory = PublicOS
endmodule

module Privileges (
  input  [15:0] in_1,
  input  in_2,
  input  in_3,
  input  in_4,
  input  in_5,
  output New_Flags
);

  wire comparator_1_eq, comparator_2_eq, comparator_3_eq, comparator_4_eq, d_ff_2_qn, multiplexer_1_out,
       or_1_out, Privledges, Reset;

  Comparator #(.width(16)) comparator_1 (.a(in_1), .b(16'h410e), .eq(comparator_1_eq));  // open: gt, lt
  Comparator #(.width(16)) comparator_2 (.a(16'he00a), .b(in_1), .eq(comparator_2_eq));  // open: gt, lt
  Comparator #(.width(16)) comparator_3 (.a(16'he008), .b(in_1), .eq(comparator_3_eq));  // open: gt, lt
  Comparator #(.width(16)) comparator_4 (.a(16'he009), .b(in_1), .eq(comparator_4_eq));  // open: gt, lt
  D_Flip_Flop d_ff_1 (
    .clk(in_2), .D(comparator_2_eq), .Qn(Privledges), .en(comparator_2_eq), .reset(or_1_out));  // open: Q, preset
  or or_1 (or_1_out, comparator_3_eq, in_3, in_5);
  Multiplexer multiplexer_1 (.in0(Privledges), .in1(in_4), .out(multiplexer_1_out), .sel(comparator_4_eq));  // open: en
  D_Flip_Flop d_ff_2 (
    .clk(in_2), .D(comparator_4_eq), .Qn(d_ff_2_qn), .preset(comparator_1_eq), .en(comparator_4_eq),
    .reset(Reset));  // open: Q
  or or_2 (Reset, comparator_2_eq, or_1_out);
  Register #(.width(1)) register_1 (.D(multiplexer_1_out), .en(d_ff_2_qn), .Q(New_Flags), .clk(in_2));  // open: clr

  // Other names for the same wires on the sheet: CLK = in_2; Instruction[15:0] = in_1; NewPrivileges = in_4;
  //   PrivledgesOut = New_Flags; ThreadError = in_5; ThreadSwitch = in_3
endmodule
